# Fritzing sketch extruder (saved by Fritzing 0.9.3b)

parts:
  LED1 = LED - 3mm [color="Red (633nm)" package="3 mm [THT]"]
  LED2 = LED - 3mm [color="Green (555nm)" package="3 mm [THT]"]
  F1 = Fan - Ventilador [package=THT]
  F2 = Fan - Ventilador [package=THT]
  F3 = Fan - Ventilador [package=THT]
  OMRON1 = OMRON PCB Power Relay – G5LE [part_number="G5LE-1\n" package=THT]
  M1 = Stepper Motor - Bipolar
  M2 = Stepper Motor - Bipolar
  U1 = SWITCH-SPST-2 [package=switch-spst-vertical]
  U2 = SWITCH-SPST-2 [package=switch-spst-vertical]
  U3 = SWITCH-SPST-2 [package=switch-spst-vertical]
  S4 = Pushbutton [package="[SMD]"]
  S5 = SWITCH-SPST-2 [package=r_sw_th]
  U4 = SWITCH-SPST-2 [package=switch-spst-vertical]
  R1 = Resistor [tolerance=±5% resistance=0 package="0805 [SMD]"]
  OMRON2 = OMRON PCB Power Relay – G5LE [part_number="G5LE-1\n" package=THT]
  JACK1 = 2.1mm Barrel Jack with Terminal Block
  JACK2 = 2.1mm Barrel Jack with Terminal Block
  R2 = Temperature Sensor (Thermistor) [thermistor_type=NTC package=THT]
  R3 = Resistor [tolerance=±1% resistance=10k package="2010 [SMD]"]
  U5 = SWITCH-SPST-2 [package=switch-spst-vertical]
  Part4 = EasyDriver_v44
  Part5 = EasyDriver_v44
  Part3 = Arduino Mega 2560 (Rev3)

nets:
  N1: LED1.cathode, LED2.cathode, OMRON1.COIL1, U1.P, U2.P, U3.P, S4.Pin_3, S4.Pin_4, U4.P, OMRON2.COIL1, R3.Pin_1, U5.P, Part3.GND, Part3.D13_PWM
  N2: LED1.anode, Part3.D11_PWM
  N3: LED2.anode, Part3.D12_PWM
  5V: F1.5V, F2.5V, F3.5V, S5.P, Part4.V+, Part5.V+
  GND: F1.GND, OMRON1.B, JACK2.POS, Part4.GND, Part5.GND
  GND_2: F2.GND, F3.GND, OMRON1.C
  N4: OMRON1.COIL2, Part3.D10_PWM
  N5: M1.A, Part4.OUT2A
  N6: M1.C, Part4.OUT2B
  N7: M1.B, Part4.OUT1A
  N8: M1.D, Part4.OUT1B
  N9: M2.A, Part5.OUT2A
  N10: M2.C, Part5.OUT2B
  N11: M2.B, Part5.OUT1A
  N12: M2.D, Part5.OUT1B
  N13: U1.O, Part3.D22
  VCC: U2.O, U4.O, R2.pin_1, Part4.VCC, Part5.VCC, Part3.5V
  N14: U3.O, Part3.D24
  N15: S5.O, JACK2.NEG
  N16: R1.Pin_0, OMRON2.B
  N17: R1.Pin_1, JACK1.POS
  N18: OMRON2.C, JACK1.NEG
  N19: OMRON2.COIL2, Part3.D28
  N20: R2.pin_0, R3.Pin_0, Part3.A0
  N21: U5.O, Part3.D23
  N22: Part4.STEP, Part3.D6_PWM
  N23: Part4.DIR, Part3.D5_PWM
  N24: Part4.ENABLE, Part3.D7_PWM
  N25: Part5.STEP, Part3.D3_PWM
  N26: Part5.DIR, Part3.D2_PWM
  N27: Part5.ENABLE, Part3.D4_PWM

notes:
  Indicadors temperatura fred/calent
  Refrigeració filament
  Refrigeració continua placa base
  Placa base Arduino Mega 2650
  Motor de passos: extrusor
  Motor de passos: bobina
  Int: General
  Int: Refrigeració filament
  Int: Extrusió
  Int: Invertir direcció
  PBtn: Emergency STOP
  Int: Habilitar recullidor
  Controladores motors
  tb6600
  Font d'alimentació 12V DC
  Relé circuit refrigeració
  Relé d'Estat Sòlid per la resistència
  Resistènica per escalfar
  NTC
  Adaptador corrent AC-DC 220V
  Int: Escalfar

custom parts:
  Fan - Ventilador: Ventilador de 2 pines, se encuentra comunmente en computadoras de escritorio

// code stored in the sketch: .ino
/*

  Extrusora de PLA controlada per Arduino Mega 2560.

  Projecte: 
  - https://github.com/bertugarangou/ExtrusoraPLA

  Circuit:
  - Extrusora feta per Albert Garangou,
    com a Treball de Recerca a 2n de Batxillerat,
    curs 2018/2019, tutor Jordi Fanals Oriol,
    codi amb Arduino IDE 1.8.5,

    Copyright (c) 2018 Albert Garangou Culebras (albertgarangou@gmail.com)
    This Font Software is licensed under the SIL Open Font License, Version 1.1.

*/
